# Fritzing sketch AirPump_5V_InflateOnly (saved by Fritzing 0.9.3b)

parts:
  Part1 = Arduino Uno (Rev3)
  Power_plug1 = Power plug
  M1 = DC Motor
  Part2 = IFR520 MOS module [package=THT]
  LED1 = smd LED [color="Red (633nm)" package="0603 [SMD]"]

nets:
  N1: Part1.D13/SCK, LED1.anode
  N2: Part1.GND, Part2.pin3, LED1.cathode
  N3: Part1.D3_PWM, Part2.pin1
  N4: Part1.5V, Part2.pin2
  N5: Power_plug1.GND, Part2.pin7
  N6: Power_plug1.VCC, Part2.pin6
  N7: M1.pin_1, Part2.pin4
